# Fritzing sketch pcb1 (saved by Fritzing 1.0.6)
circuit board: 6.70593cm x 5.84447cm
breadboards: 2

parts:
  J3 = Camdenboss CTB0158-2 [part_number=CTB0158-2 package=THT]
  J4 = Camdenboss CTB0158-7 [part_number=CTB0158-7 package=THT]
  U1 = ESP32S-HiLetgo [part_number=ESP32S-HiLetgo]
  J5 = Camdenboss CTB0158-6 [part_number=CTB0158-6 package=THT]

nets:
  N1: J3.pin1, J3.pin2, U1.GND
  N2: J4.pin1, U1.GPIO13
  N3: J4.pin2, U1.GPIO12
  N4: J4.pin3, U1.GPIO14
  N5: J4.pin4, U1.GPIO27
  N6: J4.pin5, U1.GPIO26
  N7: J4.pin6, U1.GPIO33
  N8: J4.pin7, U1.GPIO32
  N9: U1.GPIO15, J5.pin6
  N10: U1.GPIO4, J5.pin5
  N11: U1.GPIO16, J5.pin4
  N12: U1.GPIO17, J5.pin3
  N13: U1.GPIO5, J5.pin2
  N14: U1.GPIO18, J5.pin1

notes:
  GND
  EN
  wle
  in3
  men
  in1
  in4
  mq
  in2
  UXBD
  CENTER ESP32
  tr1
  ds18
  ech1
  tr2
  dht
  ech2

custom parts:
  ESP32S-HiLetgo: HiLetgo ESP-WROOM-32 ESP32 ESP-32S Development Board 2.4GHz Dual-Mode WiFi + Bluetooth Dual Cores Microcontroller The ESP32 integrated with Antenna switches, RF Balun, power amplifiers, low-noise amplifiers, filters, and management modules, and the entire solution occupies the least area of PCB. 2.4 GHz Wi-Fi plus Bluetooth dual-mode chip, with TSMC Ultra-low power consumption 40nm technology,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
