# Fritzing sketch pcb2 (saved by Fritzing 1.0.6)
circuit board: 11.4039cm x 8.61704cm
breadboards: 1

parts:
  U2 = LuaNode32 / ESP32 [part_number=ESP32S-PIN30]
  DHT1 = DHT22 Humidity and Temperature Sensor
  Part1 = Arduino Uno (Rev3)
  J2 = Camdenboss CTB0158-10 [part_number=CTB0158-10 package=THT]
  J3 = Camdenboss CTB0158-2 [part_number=CTB0158-2 package=THT]
  J1 = Camdenboss CTB0158-2 [part_number=CTB0158-2 package=THT]

nets:
  N1: U2.D34, J2.pin10
  N2: U2.D35, J2.pin9
  N3: U2.D32, J2.pin8
  N4: U2.D33, J2.pin7
  N5: U2.D25, J2.pin6
  N6: U2.D26, J2.pin5
  N7: U2.D27, J2.pin4
  N8: U2.D14, J2.pin3
  N9: U2.D12, J2.pin2
  N10: U2.D13, J2.pin1
  GND: U2.GND, DHT1.GND, Part1.GND, J3.pin2, J1.pin1, J1.pin2
  N11: U2.RX2, Part1.D1/TX
  N12: U2.TX2, Part1.D0/RX
  VDD: DHT1.VDD, Part1.5V
  N13: DHT1.DATA, Part1.D4
  N14: Part1.3V3, J3.pin1

notes:
  3v3
  gnd
  ----
  esp32
  arduino
  dht22
  extra pins of esp

custom parts:
  LuaNode32 / ESP32: New Image for LuaNode32 DOIT ESP32 DEVKIT V1. Base parts from LuaNode32 / ESP32 ESP32 based LuaNode32 by G.Noorlander DOIT Esp32 DevKit v1 (30 pins long, 11 pins width) by Werner Rothschopf (modified by vanepp Dec 2018)
